# Fritzing sketch airplane (saved by Fritzing 0.9.3b)
breadboards: 1

parts:
  J1 = Basic Servo  # not connected
  J2 = Basic Servo  # not connected
  Part1 = Arduino Nano (Rev3.0)
  Power_plug1 = Power plug
  Part3 = NRF24L01+ Breakout Board  # not connected

nets:
  GND: Part1.GND, Power_plug1.GND
  VIN: Part1.VIN, Power_plug1.VCC

notes:
  Power plug represents battery:
  Redox 2200mAh, 11,1V/20C
